# Fritzing sketch schema (saved by Fritzing 0.9.6b)
breadboards: 1

parts:
  Composant1 = Arduino Uno (Rev3)
  U1 = RF-LINK_TX [package=rf-link_tx]
  S1 = SWITCH-MOMENTARY-2 [package=tactile-pth-12mm]
  LED1 = LED - 5mm [color="Green (565nm)" package="5 mm [THT]"]
  R1 = Resistor [tolerance=±5% resistance=220 package="0805 [SMD]"]

nets:
  N1: Composant1.D4, U1.DATA
  N2: Composant1.D5_PWM, R1.Pin_1
  N3: Composant1.D6_PWM, S1.2
  5V: Composant1.5V, U1.+5V
  GND: Composant1.GND, U1.GND, S1.1, LED1.cathode
  N4: LED1.anode, R1.Pin_0
